// Logisim project FWGC.circ as structural Verilog: 2 circuits, main circuit main
module main (
);

  wire and_1_out, and_2_out, and_3_out, and_4_out, and_5_out, C_out, check_if_legal_1_out_17,
       check_if_legal_1_out_18, check_if_legal_1_out_19, check_if_legal_1_out_20, clock_1_out, F_out, G_out,
       multiplexer_1_out, multiplexer_2_out, multiplexer_3_out, multiplexer_4_out, not_1_out, not_2_out,
       not_3_out, not_4_out, not_5_out, not_6_out, not_7_out, not_8_out, or_1_out, or_2_out, register_1_q,
       register_2_q, register_3_q, register_4_q, W_out;

  not not_1 (not_1_out, register_1_q);
  not not_2 (not_2_out, register_2_q);
  not not_3 (not_3_out, register_3_q);
  not not_4 (not_4_out, register_4_q);
  LED led_1 (.in(register_1_q));
  LED led_2 (.in(not_1_out));
  LED led_3 (.in(not_2_out));
  LED led_4 (.in(register_2_q));
  LED led_5 (.in(register_3_q));
  LED led_6 (.in(not_3_out));
  LED led_7 (.in(register_4_q));
  LED led_8 (.in(not_4_out));
  LED led_9 (.in(and_1_out));
  LED led_10 (.in(and_1_out));
  LED led_11 (.in(and_1_out));
  and and_1 (and_1_out, register_4_q, register_3_q, register_2_q, register_1_q);
  LED led_12 (.in(and_1_out));
  LED led_13 (.in(and_1_out));
  LED led_14 (.in(and_1_out));
  LED led_15 (.in(and_1_out));
  Check_if_legal check_if_legal_1 (
    .F(register_1_q), .W(register_2_q), .G(register_3_q), .C(register_4_q), .F_2(register_1_q),
    .W_2(register_2_q), .G_2(register_3_q), .C_2(register_4_q), .F_3(register_1_q), .W_3(register_2_q),
    .G_3(register_3_q), .C_3(register_4_q), .F_4(register_1_q), .W_4(register_2_q), .G_4(register_3_q),
    .C_4(register_4_q), .out_17(check_if_legal_1_out_17), .out_18(check_if_legal_1_out_18),
    .out_19(check_if_legal_1_out_19), .out_20(check_if_legal_1_out_20));
  or or_1 (or_1_out, and_3_out, and_5_out, and_4_out, and_2_out);
  Register #(.width(1)) register_1 (
    .D(multiplexer_2_out), .en(or_1_out), .Q(register_1_q), .clk(clock_1_out));  // open: clr
  Register #(.width(1)) register_2 (
    .D(multiplexer_3_out), .en(and_2_out), .Q(register_2_q), .clk(clock_1_out));  // open: clr
  Register #(.width(1)) register_3 (
    .D(multiplexer_4_out), .en(and_4_out), .Q(register_3_q), .clk(clock_1_out));  // open: clr
  Register #(.width(1)) register_4 (
    .D(multiplexer_1_out), .en(and_5_out), .Q(register_4_q), .clk(clock_1_out));  // open: clr
  Button F (.out(F_out));
  and and_2 (and_2_out, check_if_legal_1_out_18, W_out);
  and and_3 (and_3_out, check_if_legal_1_out_17, F_out);
  or or_2 (or_2_out, and_3_out, and_2_out, and_4_out, and_5_out);
  Clock #(.lowDuration(10)) clock_1 (.out(clock_1_out));
  not not_5 (not_5_out, register_4_q);
  Multiplexer #(.enable("false")) multiplexer_1 (
    .in0(register_4_q), .in1(not_5_out), .out(multiplexer_1_out), .sel(and_5_out));
  Button W (.out(W_out));
  Button G (.out(G_out));
  and and_4 (and_4_out, check_if_legal_1_out_19, G_out);
  not not_6 (not_6_out, register_1_q);
  Multiplexer #(.enable("false")) multiplexer_2 (
    .in0(register_1_q), .in1(not_6_out), .out(multiplexer_2_out), .sel(or_2_out));
  not not_7 (not_7_out, register_2_q);
  Multiplexer #(.enable("false")) multiplexer_3 (
    .in0(register_2_q), .in1(not_7_out), .out(multiplexer_3_out), .sel(and_2_out));
  Multiplexer #(.enable("false")) multiplexer_4 (
    .in0(register_3_q), .in1(not_8_out), .out(multiplexer_4_out), .sel(and_4_out));
  Button C (.out(C_out));
  and and_5 (and_5_out, check_if_legal_1_out_20, C_out);
  not not_8 (not_8_out, register_3_q);

  // Notes on the sheet:
  //   Click one of the buttons to make a move
  //   If it was a legal move, you will see the positions update
  //   If you complete the game, the colorful LED'S will light up
  //   Make sure clock simulation is on, and the tick frequency is high
  //   Welcome to the Farmer Wolf Goat Cabbage Problem
  //   check if legal
endmodule

module Check_if_legal (
  input  F,
  input  W,
  input  G,
  input  C,
  input  F_2,
  input  W_2,
  input  G_2,
  input  C_2,
  input  F_3,
  input  W_3,
  input  G_3,
  input  C_3,
  input  F_4,
  input  W_4,
  input  G_4,
  input  C_4,
  output out_17,
  output out_18,
  output out_19,
  output out_20
);

  wire and_1_out, and_2_out, and_3_out, and_4_out, and_5_out, and_6_out, and_7_out, and_8_out, and_9_out,
       and_10_out, and_11_out, and_12_out, and_13_out, and_14_out, and_15_out, and_16_out, and_17_out,
       and_18_out, and_19_out, and_20_out, not_1_out, not_2_out, not_3_out, not_4_out, not_5_out, not_6_out,
       not_7_out, not_8_out, not_9_out, not_10_out, not_11_out, not_12_out, not_13_out, not_14_out,
       not_15_out, not_16_out, not_17_out, not_18_out, not_19_out, not_20_out, not_21_out, not_22_out,
       not_23_out, not_24_out, not_25_out, not_26_out, not_27_out, not_28_out, not_29_out, not_30_out,
       not_31_out, not_32_out, not_33_out, not_34_out, not_35_out, not_36_out, not_37_out, not_38_out,
       not_39_out, not_40_out;

  not not_1 (not_1_out, F);
  not not_2 (not_2_out, W);
  not not_3 (not_3_out, C);
  not not_4 (not_4_out, F);
  not not_5 (not_5_out, G);
  not not_6 (not_6_out, W);
  not not_7 (not_7_out, C);
  not not_8 (not_8_out, G);
  not not_9 (not_9_out, C_2);
  not not_10 (not_10_out, G_2);
  not not_11 (not_11_out, F_2);
  not not_12 (not_12_out, W_2);
  not not_13 (not_13_out, C_2);
  not not_14 (not_14_out, F_2);
  not not_15 (not_15_out, W_2);
  not not_16 (not_16_out, G_2);
  not not_17 (not_17_out, F_3);
  not not_18 (not_18_out, W_3);
  not not_19 (not_19_out, G_3);
  not not_20 (not_20_out, C_3);
  not not_21 (not_21_out, F_3);
  not not_22 (not_22_out, W_3);
  not not_23 (not_23_out, G_3);
  not not_24 (not_24_out, F_3);
  not not_25 (not_25_out, G_3);
  not not_26 (not_26_out, C_3);
  not not_27 (not_27_out, F_3);
  not not_28 (not_28_out, G_3);
  not not_29 (not_29_out, W_3);
  not not_30 (not_30_out, C_3);
  not not_31 (not_31_out, C_3);
  not not_32 (not_32_out, W_3);
  not not_33 (not_33_out, F_4);
  not not_34 (not_34_out, W_4);
  not not_35 (not_35_out, C_4);
  not not_36 (not_36_out, F_4);
  not not_37 (not_37_out, G_4);
  not not_38 (not_38_out, C_4);
  not not_39 (not_39_out, G_4);
  not not_40 (not_40_out, W_4);
  and and_1 (and_1_out, not_1_out, not_2_out, G, not_3_out);
  and and_2 (and_2_out, not_4_out, W, not_5_out, C);
  and and_3 (and_3_out, F, not_6_out, G, not_7_out);
  and and_4 (and_4_out, F, W, not_8_out, C);
  and and_5 (and_5_out, F_2, W_2, G_2, not_9_out);
  and and_6 (and_6_out, F_2, W_2, not_10_out, C_2);
  and and_7 (and_7_out, not_11_out, not_12_out, G_2, not_13_out);
  and and_8 (and_8_out, not_14_out, not_15_out, not_16_out, C_2);
  and and_9 (and_9_out, not_17_out, not_18_out, not_19_out, not_20_out);
  and and_10 (and_10_out, not_21_out, not_22_out, not_23_out, C_3);
  and and_11 (and_11_out, not_24_out, W_3, not_25_out, not_26_out);
  and and_12 (and_12_out, not_27_out, W_3, not_28_out, C_3);
  and and_13 (and_13_out, F_3, not_29_out, G_3, not_30_out);
  and and_14 (and_14_out, F_3, W_3, G_3, not_31_out);
  and and_15 (and_15_out, F_3, W_3, G_3, C_3);
  and and_16 (and_16_out, F_3, not_32_out, G_3, C_3);
  and and_17 (and_17_out, not_33_out, not_34_out, G_4, not_35_out);
  and and_18 (and_18_out, not_36_out, W_4, not_37_out, not_38_out);
  and and_19 (and_19_out, F_4, W_4, not_39_out, C_4);
  and and_20 (and_20_out, F_4, not_40_out, G_4, C_4);
  or or_1 (out_17, and_1_out, and_2_out, and_3_out, and_4_out);
  or or_2 (out_18, and_5_out, and_6_out, and_7_out, and_8_out);
  or or_3 (out_20, and_17_out, and_18_out, and_19_out, and_20_out);
  or or_4 (out_19, and_11_out, and_9_out, and_10_out, and_12_out, and_13_out, and_14_out, and_15_out, and_16_out);

  // Notes on the sheet:
  //   check if takesCab legal
  //   Check if goesAlone is legal
  //   check if takesWolf is legal
  //   check if takesGoat is legal
endmodule
