// Logisim project asdf.circ as structural Verilog: 2 circuits, main circuit main
module main (
  input  in_1,
  input  in_2,
  input  in_3,
  input  in_4
);

  wire clock_1_out, not_1_out, not_2_out, not_3_out, not_4_out, register_1_q, register_2_q, register_3_q,
       register_4_q;

  Button F ();  // open: out
  Button W ();  // open: out
  Button G ();  // open: out
  Button C ();  // open: out
  LED led_1 (.in(not_1_out));
  not not_1 (not_1_out, register_1_q);
  not not_2 (not_2_out, register_2_q);
  LED led_2 (.in(not_2_out));
  not not_3 (not_3_out, register_3_q);
  LED led_3 (.in(not_3_out));
  not not_4 (not_4_out, register_4_q);
  LED led_4 (.in(not_4_out));
  LED led_5 (.in(register_1_q));
  LED led_6 (.in(register_2_q));
  LED led_7 (.in(register_3_q));
  LED led_8 (.in(register_4_q));
  Check_if_legal check_if_legal_1 ();  // open: F, W, G, C, F_2, W_2, G_2, C_2, F_3, W_3, G_3, C_3, F_4, W_4, G_4, C_4, out_17, out_18, out_19, out_20
  Register #(.width(1)) register_1 (.D(in_1), .en(1'b1), .Q(register_1_q), .clk(clock_1_out));  // open: clr
  Register #(.width(1)) register_2 (.D(in_2), .en(1'b1), .Q(register_2_q), .clk(clock_1_out));  // open: clr
  Clock clock_1 (.out(clock_1_out));
  Register #(.width(1)) register_3 (.D(in_3), .en(1'b1), .Q(register_3_q), .clk(clock_1_out));  // open: clr
  Register #(.width(1)) register_4 (.D(in_4), .en(1'b1), .Q(register_4_q), .clk(clock_1_out));  // open: clr

  // Notes on the sheet:
  //   check if legal
endmodule

module Check_if_legal (
  input  F,
  input  W,
  input  G,
  input  C,
  input  F_2,
  input  W_2,
  input  G_2,
  input  C_2,
  input  F_3,
  input  W_3,
  input  G_3,
  input  C_3,
  input  F_4,
  input  W_4,
  input  G_4,
  input  C_4,
  output out_17,
  output out_18,
  output out_19,
  output out_20
);

  wire and_1_out, and_2_out, not_1_out, not_2_out, not_3_out, not_4_out, not_5_out, not_6_out, not_7_out,
       not_8_out, not_9_out, not_10_out, not_11_out, not_12_out, not_13_out, not_14_out, or_1_out, or_2_out,
       or_3_out, or_4_out, or_5_out, or_6_out, or_7_out, or_8_out, or_9_out, or_10_out, or_11_out, or_12_out;

  not not_1 (not_1_out, G);
  not not_2 (not_2_out, F);
  or or_1 (or_1_out, not_1_out, W, C);
  or or_2 (or_2_out, F, not_3_out);
  not not_3 (not_3_out, G);
  or or_3 (or_3_out, F, not_4_out);
  not not_4 (not_4_out, W);
  or or_4 (or_4_out, W, not_2_out);
  not not_5 (not_5_out, W_2);
  not not_6 (not_6_out, C_2);
  not not_7 (not_7_out, C_2);
  not not_8 (not_8_out, G_2);
  and and_1 (and_1_out, F_3, G_3);
  not not_9 (not_9_out, F_3);
  and and_2 (and_2_out, not_9_out, not_10_out);
  not not_10 (not_10_out, G_3);
  or or_5 (or_5_out, C_4, not_11_out);
  not not_11 (not_11_out, F_4);
  or or_6 (or_6_out, F_4, not_12_out);
  not not_12 (not_12_out, C_4);
  or or_7 (or_7_out, G_4, W_4);
  not not_13 (not_13_out, W_4);
  or or_8 (or_8_out, not_13_out, not_14_out);
  not not_14 (not_14_out, W_4);
  or or_9 (or_9_out, G_2, C_2);
  or or_10 (or_10_out, F_2, not_5_out);
  or or_11 (or_11_out, W_2, not_6_out);
  or or_12 (or_12_out, not_7_out, not_8_out);
  nand nand_1 (out_17, or_1_out, or_2_out, or_3_out, or_4_out);
  and and_3 (out_18, or_9_out, or_10_out, or_11_out, or_12_out);
  or or_13 (out_19, and_1_out, and_2_out);
  and and_4 (out_20, or_5_out, or_6_out, or_7_out, or_8_out);

  // Notes on the sheet:
  //   Check if goesAlone is legal
  //   check if takesWolf is legal
  //   check if takesGoat is legal
  //   check if takesCab legal
endmodule
